# Fritzing sketch AnalogClockBreadboard (saved by Fritzing 0.9.3b)
breadboards: 1

parts:
  Arduino_Nano = Arduino Nano (Rev3.0) (ICSP)
  BT-Module = Bluetooth HC-05 Macho
  Temperature&_Humidity_Sensor = DHT11 Humitidy and Temperature Sensor
  R1 = Resistor [tolerance=±5% resistance=10k package=THT]
  R2 = Resistor [tolerance=±5% resistance=1k package=THT]
  R3 = Resistor [tolerance=±5% resistance=2.2k package=THT]
  part = ws2812b [package="smd 2812b"]
  part_2 = ws2812b [package="smd 2812b"]
  24*RGB = ws2812b [package="smd 2812b"]
  R4 = Resistor [tolerance=±5% resistance=330 package="2010 [SMD]"]
  Real_Time_Clock = ZS-042 RTC Module
  4*7s_display = Grove 4 Digit Display
  Power_Supply = Mini-USB _B_ connector with 5th pin broken out. [package=usb-micro_b]

nets:
  GND: Arduino_Nano.GND, BT-Module.GND, Temperature&_Humidity_Sensor.GND, R3.Pin_1, part.VSS, part_2.VSS, 24*RGB.VSS, Real_Time_Clock.GND, 4*7s_display.GND, Power_Supply.D-
  N1: Arduino_Nano.D2, 4*7s_display.CLK
  N2: Arduino_Nano.D3, 4*7s_display.DIO
  N3: Arduino_Nano.D6, R4.Pin_1
  N4: Arduino_Nano.D8, BT-Module.TXD
  N5: Arduino_Nano.D9, R2.Pin_0
  N6: Arduino_Nano.D12/MISO, Temperature&_Humidity_Sensor.DATA, R1.Pin_0
  VDD: Arduino_Nano.VIN, BT-Module.VCC, Temperature&_Humidity_Sensor.VDD, R1.Pin_1, part.VDD, part_2.VDD, 24*RGB.VDD, Real_Time_Clock.VCC, 4*7s_display.VCC, Power_Supply.VBUS
  N7: Arduino_Nano.A5, Real_Time_Clock.SCL
  N8: Arduino_Nano.A4, Real_Time_Clock.SDA
  N9: BT-Module.RXD, R2.Pin_1, R3.Pin_0
  N10: part.DIN, part_2.DOUT
  N11: part_2.DIN, 24*RGB.DOUT
  N12: 24*RGB.DIN, R4.Pin_0

notes:
  WS2812B LED strip (etc.)
  Step up module & battery
  Use the other Schema!

custom parts:
  DHT11 Humitidy and Temperature Sensor: DHT11 Humidity and Temperature Sensor

// code stored in the sketch: AnalogClockV4.ino
/** made for AnalogClockV4.ino
 *  @see [ https://github.com/Schn33W0lf/24-Segment-Analog-Clock/blob/master/AnalogClockV4.ino] for the current version
 *   by Schn33W0lf
 */
