# Fritzing sketch AnalogClockV1 (saved by Fritzing 0.9.3b)
circuit board: 9cm x 5.1cm
perfboards: 1

parts:
  24*RGB = ws2812b [package="smd 2812b"]
  BT-Module = Bluetooth HC-05 Macho
  4*7s_display = Grove 4 Digit Display
  R4_1 = Resistor [tolerance=±5% resistance=1k package=THT]
  Real_Time_Clock = ZS-042 RTC Module
  part = ws2812b [package="smd 2812b"]
  R1_1 = Resistor [tolerance=±5% resistance=10k package=THT]
  R4_2 = Resistor [tolerance=±5% resistance=2.2k package=THT]
  part_2 = ws2812b [package="smd 2812b"]
  Arduino_Nano = Arduino Nano (Rev3.0) (ICSP)
  J1_2 = male pin header, 4 pins [form="♂ (male)"]
  J2_1 = female pin header, 4 pins [form="♀ (female)"]
  J2_2 = male pin header, 4 pins [form="♂ (male)"]
  J3_1 = female pin header, 4 pins [form="♀ (female)"]
  J3_2 = male pin header, 4 pins [form="♂ (male)"]
  J4_1 = female pin header, 4 pins [form="♀ (female)"]
  J4_2 = male pin header, 4 pins [form="♂ (male)"]
  J5_1 = female pin header, 3 pins [form="♀ (female)"]
  J5_2 = male pin header, 3 pins [form="♂ (male)"]
  J0_1_1 = female pin header, 15 pins [form="♀ (female)"]
  J0_1_2 = male pin header, 15 pins [form="♂ (male)"]
  J0_2_2 = male pin header, 15 pins [form="♂ (male)"]
  J0_2_1 = female pin header, 15 pins [form="♀ (female)"]
  R5_1 = Resistor [tolerance=±5% resistance=330 package=THT]
  J1_1 = female pin header, 4 pins [form="♀ (female)"]
  DHT1 = DHT11 Humitidy and Temperature Sensor
  Power_plug_(5V_) = Power plug
  0V = Pad [width=3 height=2 connect=center]
  +5V = Pad [width=3 height=2 connect=center]

nets:
  VDD: 24*RGB.VDD, part.VDD, part_2.VDD, J5_2.pin1
  N1: 24*RGB.DOUT, part.DIN
  VSS: 24*RGB.VSS, part.VSS, part_2.VSS, J5_2.pin3
  N2: 24*RGB.DIN, J5_2.pin2
  N3: BT-Module.TXD, J4_2.pin3
  N4: BT-Module.RXD, J4_2.pin4
  N5: BT-Module.VCC, J4_2.pin1
  N6: BT-Module.GND, J4_2.pin2
  N7: 4*7s_display.GND, J3_2.pin1
  N8: 4*7s_display.VCC, J3_2.pin2
  N9: 4*7s_display.DIO, J3_2.pin3
  N10: 4*7s_display.CLK, J3_2.pin4
  N11: R4_1.Pin_0, J0_1_1.pin12
  N12: R4_1.Pin_1, R4_2.Pin_1, J4_1.pin2
  N13: Real_Time_Clock.GND, J2_2.pin1
  N14: Real_Time_Clock.VCC, J2_2.pin2
  N15: Real_Time_Clock.SDA, J2_2.pin3
  N16: Real_Time_Clock.SCL, J2_2.pin4
  N17: part.DOUT, part_2.DIN
  N18: R1_1.Pin_0, R4_2.Pin_0, J2_1.pin4, J3_1.pin4, J4_1.pin3, J5_1.pin3, J0_1_1.pin4, J1_1.pin4, Power_plug_(5V_).GND, 0V.pad
  N19: R1_1.Pin_1, J0_1_1.pin15, J1_1.pin2
  N20: Arduino_Nano.D1/TX, J0_1_2.pin1
  N21: Arduino_Nano.D0/RX, J0_1_2.pin2
  N22: Arduino_Nano.RESET, J0_1_2.pin3, J0_2_2.pin3
  N23: Arduino_Nano.GND, J0_1_2.pin4, J0_2_2.pin2
  N24: Arduino_Nano.D2, J0_1_2.pin5
  N25: Arduino_Nano.D3, J0_1_2.pin6
  N26: Arduino_Nano.D4, J0_1_2.pin7
  N27: Arduino_Nano.D5, J0_1_2.pin8
  N28: Arduino_Nano.D6, J0_1_2.pin9
  N29: Arduino_Nano.D7, J0_1_2.pin10
  N30: Arduino_Nano.D8, J0_1_2.pin11
  N31: Arduino_Nano.D9, J0_1_2.pin12
  N32: Arduino_Nano.D10, J0_1_2.pin13
  N33: Arduino_Nano.D11/MOSI, J0_1_2.pin14
  N34: Arduino_Nano.D12/MISO, J0_1_2.pin15
  N35: Arduino_Nano.VIN, J0_2_2.pin1
  N36: Arduino_Nano.5V, J0_2_2.pin4
  N37: Arduino_Nano.A7, J0_2_2.pin5
  N38: Arduino_Nano.A6, J0_2_2.pin6
  N39: Arduino_Nano.A5, J0_2_2.pin7
  N40: Arduino_Nano.A4, J0_2_2.pin8
  N41: Arduino_Nano.A3, J0_2_2.pin9
  N42: Arduino_Nano.A2, J0_2_2.pin10
  N43: Arduino_Nano.A1, J0_2_2.pin11
  N44: Arduino_Nano.A0, J0_2_2.pin12
  N45: Arduino_Nano.AREF, J0_2_2.pin13
  N46: Arduino_Nano.3V3, J0_2_2.pin14
  N47: Arduino_Nano.D13/SCK, J0_2_2.pin15
  N48: J1_2.pin1, DHT1.GND
  N49: J1_2.pin2, DHT1.NULL
  N50: J1_2.pin3, DHT1.DATA
  N51: J1_2.pin4, DHT1.VDD
  N52: J2_1.pin1, J0_2_1.pin7
  N53: J2_1.pin2, J0_2_1.pin8
  N54: J2_1.pin3, J3_1.pin3, J4_1.pin4, J5_1.pin1, J0_2_1.pin1, J1_1.pin1, Power_plug_(5V_).VCC, +5V.pad
  N55: J3_1.pin1, J0_1_1.pin5
  N56: J3_1.pin2, J0_1_1.pin6
  N57: J4_1.pin1, J0_1_1.pin11
  N58: J5_1.pin2, R5_1.Pin_0
  N59: J0_1_1.pin9, R5_1.Pin_1

notes:
  24x WS2812B
  (only tested with those, others should work either)
  J0.2.2 & J0.1.2 are the arduino pins
  AnalogClockV1

custom parts:
  DHT11 Humitidy and Temperature Sensor: DHT11 Humidity and Temperature Sensor
